# Fritzing sketch rgb_led_text (saved by Fritzing 0.9.3b)
breadboards: 1

parts:
  R1 = Resistor [tolerance=±5% resistance=330 package=THT]
  LED1 = RGB LED (com. cathode, rgb) [package="5 mm [THT]"]
  R2 = Resistor [tolerance=±5% resistance=330 package=THT]  # not connected
  R3 = Resistor [tolerance=±5% resistance=330 package=THT]
  Componente1 = Arduino Uno (Rev3)

nets:
  N1: R1.Pin_0, Componente1.D9_PWM
  N2: R1.Pin_1, LED1.red_anode
  N3: LED1.common_cathode, Componente1.GND
  N4: LED1.green_anode, R3.Pin_1
  N5: R3.Pin_0, Componente1.D10_PWM/SS

notes:
  LED RGB
  Resistencias 330 Ω

// code stored in the sketch: rgb_led_text.ino
// Pins 
#define BLUE 11
#define GREEN 10
#define RED 9

// vars
long color;
int redValue;
int greenValue;
int blueValue;

void setup() {
  pinMode(RED, OUTPUT);
  pinMode(GREEN, OUTPUT);
  pinMode(BLUE, OUTPUT);
  Serial.begin(9600);
}

void loop() {
  while (Serial.available()) {
    delay(3);
    color = Serial.parseInt();
  }

  if (color != 0) {
    Serial.println(color);
    switch (color) {
      case 1:
        redValue = 255;
        greenValue = 0;
        blueValue = 0;
        switchLed();
        break;

      case 2:
        redValue = 0;
        greenValue = 0;
        blueValue = 255;
        switchLed();
        break;

       case 3:
        redValue = 0;
        greenValue = 255;
        blueValue = 0;
        switchLed();
        break;
    }
  }
}

void switchLed() {
  analogWrite(BLUE, blueValue);
  analogWrite(RED, redValue);
  analogWrite(GREEN, greenValue);
}
